# Fritzing sketch ledstair (saved by Fritzing 0.9.2b)
circuit board: 8.46667cm x 5.64444cm
perfboards: 1

parts:
  J1 = Screw terminal - 2 pins [package=THT]  # not connected
  S1 = Pushbutton [package="[THT]"]
  R1 = Resistor [tolerance=±5% resistance=10k package=THT]
  R2 = Resistor [tolerance=±5% resistance=1k package=THT]  # not connected
  Q1 = NPN-Transistor [package="TO92 [THT]"]
  JP2 = Header 10 [package=1x10-2mm-smd]
  JP3 = Header 10 [package=1x10-2mm-smd]
  JP4 = Header 6 [package=1x06_smd_straight_alt]  # not connected
  R4 = Resistor [tolerance=±5% resistance=1k package=THT]  # not connected
  R5 = Resistor [tolerance=±5% resistance=1k package=THT]
  R6 = Resistor [tolerance=±5% resistance=1k package=THT]
  R7 = Resistor [tolerance=±5% resistance=1k package=THT]  # not connected
  R8 = Resistor [tolerance=±5% resistance=1k package=THT]  # not connected
  R9 = Resistor [tolerance=±5% resistance=1k package=THT]
  R10 = Resistor [tolerance=±5% resistance=1k package=THT]  # not connected
  R11 = Resistor [tolerance=±5% resistance=1k package=THT]  # not connected
  R12 = Resistor [tolerance=±5% resistance=1k package=THT]  # not connected
  R13 = Resistor [tolerance=±5% resistance=1k package=THT]  # not connected
  R14 = Resistor [tolerance=±5% resistance=1k package=THT]  # not connected
  R15 = Resistor [tolerance=±5% resistance=1k package=THT]
  R16 = Resistor [tolerance=±5% resistance=1k package=THT]  # not connected
  R17 = Resistor [tolerance=±5% resistance=1k package=THT]
  R18 = Resistor [tolerance=±5% resistance=1k package=THT]  # not connected
  JP1 = M40 [package=1x40_offset]
  Q2 = NPN-Transistor [package="TO92 [THT]"]
  Q3 = NPN-Transistor [package="TO92 [THT]"]
  Q4 = NPN-Transistor [package="TO92 [THT]"]
  Q5 = NPN-Transistor [package="TO92 [THT]"]
  Q6 = NPN-Transistor [package="TO92 [THT]"]
  Q7 = NPN-Transistor [package="TO92 [THT]"]
  Q8 = NPN-Transistor [package="TO92 [THT]"]
  S2 = Pushbutton [package="[THT]"]
  S3 = Pushbutton [package="[THT]"]
  JP5 = Header 6 [package=1x06_smd_straight_alt]  # not connected
  R3 = Resistor [tolerance=±5% resistance=1k package=THT]
  S4 = Pushbutton [package="[THT]"]
  S5 = Pushbutton [package="[THT]"]
  S6 = Pushbutton [package="[THT]"]
  S7 = Pushbutton [package="[THT]"]
  S8 = Pushbutton [package="[THT]"]
  S9 = Pushbutton [package="[THT]"]
  S10 = Pushbutton [package="[THT]"]
  S11 = Pushbutton [package="[THT]"]
  S12 = Pushbutton [package="[THT]"]
  S13 = Pushbutton [package="[THT]"]
  S14 = Pushbutton [package="[THT]"]
  S15 = Pushbutton [package="[THT]"]
  S16 = Pushbutton [package="[THT]"]
  R19 = Resistor [tolerance=±5% resistance=10k package=THT]
  R20 = Resistor [tolerance=±5% resistance=10k package=THT]
  R21 = Resistor [tolerance=±5% resistance=10k package=THT]
  R22 = Resistor [tolerance=±5% resistance=10k package=THT]
  R23 = Resistor [tolerance=±5% resistance=10k package=THT]
  R24 = Resistor [tolerance=±5% resistance=10k package=THT]
  R25 = Resistor [tolerance=±5% resistance=10k package=THT]
  R26 = Resistor [tolerance=±5% resistance=10k package=THT]
  R27 = Resistor [tolerance=±5% resistance=10k package=THT]
  R28 = Resistor [tolerance=±5% resistance=10k package=THT]
  R29 = Resistor [tolerance=±5% resistance=10k package=THT]
  R30 = Resistor [tolerance=±5% resistance=10k package=THT]
  R31 = Resistor [tolerance=±5% resistance=10k package=THT]  # not connected
  R32 = Resistor [tolerance=±5% resistance=10k package=THT]
  R33 = Resistor [tolerance=±5% resistance=10k package=THT]  # not connected
  JP6 = M40 [package=1x40_offset]  # not connected
  LED1 = LED - 3mm [color="White (6500K)" package="3 mm [THT]"]

nets:
  N1: S1.Pin_1, S1.Pin_2
  N2: S1.Pin_3, S1.Pin_4
  N3: R1.Pin_0, JP2.2
  N4: Q1.E, JP1.1, LED1.anode
  N5: Q1.B, JP1.2, R3.Pin_1
  N6: Q1.C, JP1.3
  N7: JP2.1, R3.Pin_0
  N8: JP2.3, R20.Pin_1
  N9: JP2.4, R21.Pin_0
  N10: JP2.6, R25.Pin_1
  N11: JP2.7, R22.Pin_0
  N12: JP2.8, R23.Pin_1
  N13: JP2.9, R24.Pin_0
  N14: JP3.2, R27.Pin_1
  N15: JP3.3, R26.Pin_0
  N16: JP3.4, R29.Pin_1
  N17: JP3.5, R28.Pin_0
  N18: JP3.7, R32.Pin_1
  N19: JP3.8, R17.Pin_1
  N20: JP3.9, R30.Pin_1
  N21: JP3.10, R15.Pin_1
  N22: R5.Pin_1, JP1.6, Q2.B
  N23: R6.Pin_1, JP1.10, Q3.B
  N24: R9.Pin_1, JP1.14, Q4.B
  N25: JP1.5, Q2.E
  N26: JP1.7, Q2.C
  N27: JP1.9, Q3.E
  N28: JP1.11, Q3.C
  N29: JP1.13, Q4.E
  N30: JP1.15, Q4.C
  N31: JP1.17, Q5.E
  N32: JP1.18, Q5.B
  N33: JP1.19, Q5.C
  N34: JP1.21, Q6.E
  N35: JP1.22, Q6.B
  N36: JP1.23, Q6.C
  N37: JP1.25, Q7.E
  N38: JP1.26, Q7.B
  N39: JP1.27, Q7.C
  N40: JP1.29, Q8.E
  N41: JP1.30, Q8.B
  N42: JP1.31, Q8.C
  N43: S2.Pin_1, S2.Pin_2
  N44: S2.Pin_3, S2.Pin_4
  N45: S3.Pin_1, S3.Pin_2
  N46: S3.Pin_3, S3.Pin_4
  N47: S4.Pin_1, S4.Pin_2
  N48: S4.Pin_3, S4.Pin_4
  N49: S5.Pin_1, S5.Pin_2
  N50: S5.Pin_3, S5.Pin_4
  N51: S6.Pin_1, S6.Pin_2
  N52: S6.Pin_3, S6.Pin_4
  N53: S7.Pin_1, S7.Pin_2
  N54: S7.Pin_3, S7.Pin_4
  N55: S8.Pin_1, S8.Pin_2
  N56: S8.Pin_3, S8.Pin_4
  N57: S9.Pin_1, S9.Pin_2
  N58: S9.Pin_3, S9.Pin_4
  N59: S10.Pin_1, S10.Pin_2
  N60: S10.Pin_3, S10.Pin_4
  N61: S11.Pin_1, S11.Pin_2
  N62: S11.Pin_3, S11.Pin_4
  N63: S12.Pin_1, S12.Pin_2
  N64: S12.Pin_3, S12.Pin_4
  N65: S13.Pin_1, S13.Pin_2
  N66: S13.Pin_3, S13.Pin_4
  N67: S14.Pin_1, S14.Pin_2
  N68: S14.Pin_3, S14.Pin_4
  N69: S15.Pin_1, S15.Pin_2
  N70: S15.Pin_3, S15.Pin_4
  N71: S16.Pin_1, S16.Pin_2
  N72: S16.Pin_3, S16.Pin_4
  N73: R19.Pin_0, LED1.cathode
